# Fritzing sketch rpi-ballotbox (saved by Fritzing 0.9.2b)
breadboards: 1

parts:
  V1 = DC Power [voltage=12V]
  Switching_regulator = Voltage Regulator - 5V [part_number=PT78ST105H package="TO220 [THT]"]
  IC1 = L293D [package=THT]
  Sheet_feeder = DC Motor [part_number="HP J110a"]
  D1 = Rectifier Diode [part_number=1N4001 package="300 mil [THT]"]
  D2 = Rectifier Diode [part_number=1N4001 package="300 mil [THT]"]
  D3 = Rectifier Diode [part_number=1N4001 package="300 mil [THT]"]
  D4 = Rectifier Diode [part_number=1N4001 package="300 mil [THT]"]
  2A = Fuse with Handler [part_number=Htc-15m]
  Power_button = Pushbutton [package=THT]
  Feed_motor_sensor = PHOTOTRANSISTOR REFLECTIVE OBJECT SENSOR [part_number="HP J110a" package=qrb1114-side]
  R1 = Resistor [tolerance=±5% resistance=220 package=THT]
  R2 = Resistor [tolerance=±5% resistance=7.5k package=THT]
  Diverter_servo = Basic Servo [part_number="Futaba S3003"]
  Paper_sensor = PHOTOTRANSISTOR REFLECTIVE OBJECT SENSOR [package=qrb1114-side]
  Raspberry_Pi2 = Raspberry Pi 2
  R3 = Resistor [tolerance=±5% resistance=220 package=THT]
  R4 = Resistor [tolerance=±5% resistance=1k package=THT]
  Q1 = NPN-Transistor [part_number=2N2222A package="TO92 [THT]"]
  R5 = Resistor [tolerance=±5% resistance=120k package=THT]
  Scanner_switch = male pin header, 2 pins [form="♂ (male)"]

nets:
  N1: V1.V+, IC1.+Vmotor, D1.cathode, D2.cathode, 2A.Connector1
  GND: V1.V-, Switching_regulator.GND, IC1.0V, D3.anode, D4.anode, Power_button.leg1, Feed_motor_sensor.E, Feed_motor_sensor.K, Diverter_servo.gnd, Raspberry_Pi2.GND, R3.Pin_0, R4.Pin_0
  N2: Switching_regulator.input_voltage, 2A.Connector2
  VCC: Switching_regulator.output_voltage, IC1.+V, Diverter_servo.vcc, Raspberry_Pi2.5V
  N3: IC1.Enable_1, Raspberry_Pi2.GPIO17
  N4: IC1.In_1, Raspberry_Pi2.GPIO27
  N5: IC1.Out_1_(_Controlled_by_Enable_1_), Sheet_feeder.pin_2, D2.anode, D4.cathode
  N6: IC1.Out_2_(_Controlled_by_Enable_1_), Sheet_feeder.pin_1, D1.anode, D3.cathode
  N7: IC1.In_2, Raspberry_Pi2.GPIO22
  N8: Power_button.leg0, Raspberry_Pi2.GPIO3
  N9: Feed_motor_sensor.A, R1.Pin_1
  N10: Feed_motor_sensor.C, R2.Pin_1, Raspberry_Pi2.GPIO23
  N11: R1.Pin_0, R2.Pin_0, Paper_sensor.A, Paper_sensor.C, Raspberry_Pi2.3V3
  N12: Diverter_servo.pulse, Raspberry_Pi2.GPIO18
  N13: Paper_sensor.E, Raspberry_Pi2.GPIO24, R4.Pin_1
  N14: Paper_sensor.K, R3.Pin_1
  N15: Raspberry_Pi2.GPIO25, R5.Pin_0
  N16: Q1.E, Scanner_switch.pin2
  N17: Q1.B, R5.Pin_1
  N18: Q1.C, Scanner_switch.pin1
